# Fritzing sketch schem (saved by Fritzing 0.9.3b)
breadboards: 1

parts:
  DS1 = DS18B20 1-Wire Temperature Sensor [part_number=DS18B20]
  DS2 = DS18B20 1-Wire Temperature Sensor [part_number=DS18B20]
  DS3 = DS18B20 1-Wire Temperature Sensor [part_number=DS18B20]
  DS4 = DS18B20 1-Wire Temperature Sensor [part_number=DS18B20]
  Part1 = Arduino Uno (Rev3)
  R1 = Resistor [tolerance=±5% resistance=220 package=THT]
  GLCD_128x1 = 128 x 64 Graphic LCD
  U1 = POT_SWITCH [package=pot_pth_switch]

nets:
  GND: DS1.GND, DS2.GND, DS3.GND, DS4.GND, Part1.GND, GLCD_128x1.1_Vss, U1.G$1_A
  N1: DS1.DQ, DS2.DQ, DS3.DQ, DS4.DQ, Part1.D4, R1.Pin_0
  VDD: DS1.VDD, DS2.VDD, DS3.VDD, DS4.VDD, Part1.5V, R1.Pin_1, GLCD_128x1.2_Vdd, U1.G$2_2
  N2: Part1.D8, GLCD_128x1.14_DB7
  N3: Part1.D9_PWM, GLCD_128x1.13_DB6
  N4: Part1.D10_PWM/SS, GLCD_128x1.12_DB5
  N5: Part1.D11_PWM/MOSI, GLCD_128x1.11_DB4
  N6: Part1.D12/MISO, GLCD_128x1.6_Enable
  N7: Part1.D13/SCK, GLCD_128x1.5_R/W
  N8: GLCD_128x1.3_Vo, U1.G$2_1
